# Fritzing sketch 2s_lipo_charger (saved by Fritzing 0.9.2b)
breadboards: 1

parts:
  Load = Header 2 [package=jst-2-smd]
  FQP27P06 = Basic FET P-Channel [package="DPak [SMD]"]
  D1 = Schottky Diode [part_number=1N5817 package="Melf DO-213 AB [SMD]"]
  R1 = Resistor [tolerance=±5% resistance=1M package="2512 [SMD]"]
  External_8_4-12_6V = Header 2 [package=jst-2-smd]
  batt_discharge = Header 2 [package=jst-2-smd]
  batt_mon = Header 2 [package=jst-2-smd]

nets:
  GND: Load.2, R1.Pin_1, External_8_4-12_6V.2, batt_discharge.2, batt_mon.2
  N1: Load.1, FQP27P06.source, D1.cathode
  N2: FQP27P06.Gate, D1.anode, R1.Pin_0, External_8_4-12_6V.1
  N3: FQP27P06.drain, batt_discharge.1, batt_mon.1
