# Fritzing sketch battery_balance_cable (saved by Fritzing 0.9.2b)
breadboards: 1

parts:
  D1 = Rectifier Diode [part_number=1N4001 package="300 mil [THT]"]
  D2 = Rectifier Diode [part_number=1N4001 package="300 mil [THT]"]
  JP1 = Header 3 [part_number=Battery package=screwterminal-3.5mm-3_lock.007s]
  JP2 = Header 3 [part_number=Charger package=screwterminal-3.5mm-3_lock.007s]

nets:
  N1: D1.cathode, JP1.1
  N2: D1.anode, JP2.1
  N3: D2.cathode, JP1.2
  N4: D2.anode, JP2.2
  GND: JP1.3, JP2.3
