# Fritzing sketch battery_pack (saved by Fritzing 0.9.2b)
breadboards: 1

parts:
  V1 = DC Power [voltage=5]
  V2 = DC Power [voltage=5]
  S1 = MK22-Reed-Sensor [package=mk22-reed-sensor]

nets:
  B+: V1.V+
  B1: V1.V-, V2.V+
  B-: V2.V-, S1.2
  GND/P-: S1.1

custom parts:
  MK22-Reed-Sensor: Various NO switches- pushbuttons, reed, etc
