# Fritzing sketch battery_voltage_sensor_1 (saved by Fritzing 0.9.2b)
circuit board: 2.54676cm x 1.31512cm
breadboards: 1

parts:
  R1 = Resistor [tolerance=±5% resistance=2M package=THT]
  R2 = Resistor [tolerance=±5% resistance=1M package=THT]
  J1 = Screw terminal - 2 pins [package=THT]

nets:
  0-12V: R1.Pin_0, J1.pin2
  ADC: R1.Pin_1, R2.Pin_0
  GND: R2.Pin_1, J1.pin1
