# Fritzing sketch battery_voltage_sensor_2 (saved by Fritzing 0.9.2b)
circuit board: 2.54676cm x 1.31512cm
breadboards: 1

parts:
  Q1 = TRANSISTOR_NPN [package=to-92-ammo]
  R1 = Resistor [tolerance=±5% resistance=220 package=THT]
  R2 = Resistor [tolerance=±5% resistance=220 package=THT]
  J1 = Screw terminal - 2 pins [package=THT]
  J3 = Screw terminal - 2 pins [package=THT]

nets:
  N1: Q1.E, R1.Pin_0
  EN: Q1.B, J3.pin1
  0-12V: Q1.C, J1.pin2
  ADC: R1.Pin_1, R2.Pin_0, J3.pin2
  GND: R2.Pin_1, J1.pin1
