# Fritzing sketch battery_voltage_sensor_3 (saved by Fritzing 0.9.2b)
circuit board: 3.5cm x 1cm
breadboards: 1

parts:
  -_+ = Screw terminal - 2 pins [package=THT]
  R4 = Resistor [tolerance=±5% resistance=100 package=THT]
  R5 = Resistor [tolerance=±5% resistance=100 package=THT]
  R3 = Resistor [tolerance=±5% resistance=10k package=THT]
  R1 = Resistor [tolerance=±5% resistance=20k package=THT]
  R2 = Resistor [tolerance=±5% resistance=10k package=THT]
  R6 = Resistor [tolerance=±5% resistance=10k package=THT]
  Q1 = PNP-Transistor [package="TO92 [THT]"]
  Q2 = NPN-Transistor [package="TO92 [THT]"]
  VO_EN_GND = Header 3 [package=jst-3-pth]

nets:
  N1: -_+.pin1, R6.Pin_1, Q1.E
  GND: -_+.pin2, R3.Pin_1, R2.Pin_1, Q2.E, VO_EN_GND.3
  N2: R4.Pin_0, R6.Pin_0, Q1.B
  N3: R4.Pin_1, Q2.C
  N4: R5.Pin_0, R3.Pin_0, Q2.B
  EN: R5.Pin_1, VO_EN_GND.2
  N5: R1.Pin_0, Q1.C
  ADC: R1.Pin_1, R2.Pin_0, VO_EN_GND.1
