# Fritzing sketch head_fan (saved by Fritzing 0.9.2b)
breadboards: 1

parts:
  R1 = Resistor [tolerance=±5% resistance=330 package=THT]
  R2 = Resistor [tolerance=±5% resistance=10k package=THT]
  D1 = Rectifier Diode [part_number=1N4001 package="300 mil [THT]"]
  M1 = DC Motor [part_number="Copal F17HA"]
  Q1 = NPN-Transistor [part_number=2N4401 package="TO92 [THT]"]

nets:
  control: R1.Pin_0
  N1: R1.Pin_1, R2.Pin_0, Q1.B
  GND: R2.Pin_1, Q1.E
  5V: D1.cathode, M1.pin_1
  N2: D1.anode, M1.pin_2, Q1.C
