# Fritzing sketch head_led (saved by Fritzing 0.9.2b)
breadboards: 1

parts:
  U1 = Tri-Color LED SMD [part_number=YSL-R596CR3G4B5C-C10 package=led-tricolor-smd]
  JP1 = Header 3 [package=screwterminal-3.5mm-3_lock.007s]
  R1 = Resistor [tolerance=±5% resistance=150 package=THT]
  R2 = Resistor [tolerance=±5% resistance=90 package=THT]
  R3 = Resistor [tolerance=±5% resistance=90 package=THT]

nets:
  GND: U1.A
  N1: U1.BLU, R2.Pin_1
  N2: U1.GRN, R3.Pin_1
  N3: U1.RED, R1.Pin_1
  N4: JP1.1, R1.Pin_0
  N5: JP1.2, R2.Pin_0
  N6: JP1.3, R3.Pin_0
