# Fritzing sketch head_power_harness (saved by Fritzing 0.9.2b)
breadboards: 1

parts:
  R1 = Resistor [tolerance=±5% resistance=330 package="2010 [SMD]"]
  Q6 = Basic FET P-Channel [part_number=FQP27P06 package="TO220 [THT]"]
  Q7 = NPN-Transistor [part_number=2N4401 package="TO92 [THT]"]
  R2 = Resistor [tolerance=±5% resistance=1k package="2010 [SMD]"]
  R3 = Resistor [tolerance=±5% resistance=10k package="2010 [SMD]"]

nets:
  N1: R1.Pin_0, Q7.B
  Arduino: R1.Pin_1, R3.Pin_0
  N2: Q6.gate, Q7.C, R2.Pin_0
  Load+: Q6.drain
  Batt+: Q6.source, R2.Pin_1
  Batt-/Load-: Q7.E
  5V: R3.Pin_1
