# Fritzing sketch head_power_harness_full (saved by Fritzing 0.9.2b)
breadboards: 1

parts:
  R1 = Resistor [tolerance=±5% resistance=1k package="2010 [SMD]"]
  Raspberry_Pi1 = Raspberry Pi 2
  Part1 = Arduino Uno (Rev3)
  IC1 = Voltage Regulator [package=to-220-alt]
  X1 = USB Connectors [part_number="UNO USB" package=usb-a-h]
  X2 = USB Connectors [part_number="RPi2 USB" package=usb-a-h]
  Q6 = Basic FET P-Channel [part_number=FQP27P06 package="D2Pak [SMD]"]
  Q7 = NPN-Transistor [part_number=2N4401 package="TO92 [THT]"]
  R2 = Resistor [tolerance=±5% resistance=1k package="2010 [SMD]"]

nets:
  N1: R1.Pin_0, Q7.B
  N2: R1.Pin_1, Part1.A2
  GND: Raspberry_Pi1.GND, Part1.GND, IC1.GND, Q7.E
  N3: Raspberry_Pi1.5V, IC1.IN
  5V: Part1.5V
  N4: IC1.OUT, Q6.drain
  N5: X1.D-, X2.D-
  N6: X1.VBUS, X2.VBUS
  N7: Q6.Gate, Q7.C, R2.Pin_1
  12V: Q6.source, R2.Pin_0
