# Fritzing sketch neck_reference_sensor (saved by Fritzing 0.9.2b)
breadboards: 1

parts:
  P1 = S1133 Si Photodiode [part_number=QRD1114 package="8mm Ceramic [THT]"]
  R1 = Resistor [tolerance=±5% resistance=20k package="2010 [SMD]"]
  R2 = Resistor [tolerance=±5% resistance=25.7k package="2010 [SMD]"]

nets:
  N1: P1.cathode, R2.Pin_1
  GND: P1.anode
  5V: R1.Pin_0
  signal: R1.Pin_1, R2.Pin_0
