# Fritzing sketch power_button (saved by Fritzing 0.9.2b)
breadboards: 1

parts:
  S1 = Round Pushbutton
  LED1 = LEDs [package=led10mm]
  R1 = Resistor [tolerance=±5% resistance=1k package="0805 [SMD]"]
  D1 = Rectifier Diode [part_number=1N4001 package="300 mil [THT]"]
  D2 = Rectifier Diode [part_number=1N4001 package="300 mil [THT]"]

nets:
  GND: S1.leg0, R1.Pin_1
  N1: S1.leg1, D1.cathode, D2.cathode
  Arduino Status LED (SL): LED1.A
  N2: LED1.C, R1.Pin_0
  Pololu Pushbutton A: D1.anode
  Arduino Button Sense (SB): D2.anode
