# Fritzing sketch power_router (saved by Fritzing 0.9.2b)
circuit board: 4.3263cm x 2.25961cm
breadboards: 1

parts:
  R1 = Resistor [tolerance=±5% resistance=1M package="2010 [SMD]"]
  Q1 = Basic FET P-Channel [package="DPak [SMD]"]
  D1 = Schottky Diode [part_number=1N5817 package="Melf DO-213 AB [SMD]"]
  ext = Header 2 [package=jst-2-smd]
  batt = Header 2 [package=jst-2-smd]
  load = Header 2 [package=jst-2-smd]

nets:
  N1: R1.Pin_0, Q1.Gate, D1.anode, ext.1
  GND: R1.Pin_1, ext.2, batt.2, load.2
  N2: Q1.drain, batt.1
  N3: Q1.source, D1.cathode, load.1
