# Fritzing sketch battery charging layout (saved by Fritzing 0.9.2b)
breadboards: 1

parts:
  U1 = LIPO-1000mAh [part_number=Lipo package=lipo-1000]
  U2 = Voltage Regulator [part_number=BMS package=to220-adj]
  U3 = LIPO-1000mAh [part_number="External Power" package=lipo-1000]
  R1 = Resistor [tolerance=±5% resistance=220 part_number=Load package="1206 [SMD]"]

nets:
  N1: U1.+, U2.OUT
  GND: U1.-, U2.ADJ, U3.-, R1.Pin_1
  N2: U2.IN, U3.+, R1.Pin_0
