# Fritzing sketch recharge_plug_female_12v_v2 (saved by Fritzing 0.9.2b)
circuit board: 6.9cm x 2cm
breadboards: 1

parts:
  EP2/BV = Header 3 [package=jst-3-smd]
  R5 = Resistor [tolerance=±5% resistance=1M package="2010 [SMD]"]
  R4 = Resistor [tolerance=±5% resistance=1M package="2010 [SMD]"]
  R6 = Resistor [tolerance=±5% resistance=1M package="2010 [SMD]"]
  Load1 = Header 2 [package=jst-2-smd-vert]
  batt = Header 2 [package=jst-2-smd-vert]
  R7 = Resistor [tolerance=±5% resistance=1M package="2010 [SMD]"]
  chgr = Header 2 [package=jst-2-smd-vert]
  R3 = Resistor [tolerance=±5% resistance=1k package="2010 [SMD]"]
  EP1 = Header 2 [package=jst-2-smd-vert]
  Ext = Header 2 [package=jst-2-smd-vert]
  R2 = Resistor [tolerance=±5% resistance=1M package="2010 [SMD]"]
  R1 = Resistor [tolerance=±5% resistance=2M package="2010 [SMD]"]
  LED1 = Header 2 [package=jst-2-smd-vert]
  D1 = Diode [package=smb-diode]
  AOD4189 = Basic FET P-Channel [package="DPak [SMD]"]
  Pad3 = Pad [width=5 height=5 connect=center]  # not connected
  Pad1 = Pad [width=5 height=5 connect=center]  # not connected
  Pad4 = Pad [width=5 height=5 connect=center]  # not connected
  Pad2 = Pad [width=5 height=5 connect=center]  # not connected
  S1 = MK22-Reed-Sensor [package=mk22-reed-sensor]

nets:
  N1: EP2/BV.1, R5.Pin_0, R4.Pin_1
  GND: EP2/BV.2, R5.Pin_1, Load1.2, batt.2, R7.Pin_1, chgr.2, EP1.2, Ext.2, R2.Pin_1, LED1.2
  N2: EP2/BV.3, R6.Pin_1, R7.Pin_0
  N3: R4.Pin_0, S1.2
  N4: R6.Pin_0, batt.1, AOD4189.drain, S1.1
  N5: Load1.1, D1.C, AOD4189.source
  N6: chgr.1, R3.Pin_0, Ext.1, R1.Pin_0, D1.A, AOD4189.Gate
  N7: R3.Pin_1, LED1.1
  N8: EP1.1, R2.Pin_0, R1.Pin_1

custom parts:
  MK22-Reed-Sensor: Various NO switches- pushbuttons, reed, etc
