# Fritzing sketch circuit (saved by Fritzing 0.9.2b)
breadboards: 1

parts:
  S1 = Reed switch [package=THT]
  R1 = Resistor [tolerance=±5% resistance=20k package="0805 [SMD]"]
  R2 = Resistor [tolerance=±5% resistance=10k package="0805 [SMD]"]
  D1 = Diode [package=diode-hv]

nets:
  N1: S1.pin_1, D1.A
  Vin+: S1.pin_2, R1.Pin_0
  present: R1.Pin_1, R2.Pin_0
  GND/Vin-/Vout-: R2.Pin_1
  Vout+: D1.C
