# Fritzing sketch circuit2_smd (saved by Fritzing 0.9.2b)
circuit board: 5.0255cm x 2.01865cm
breadboards: 1

parts:
  -_+ = Screw terminal - 2 pins [package=THT]
  J1 = female pin header, 3 pins [form="♀ (female)"]
  R4 = Resistor [tolerance=±5% resistance=100 package="2512 [SMD]"]
  R1 = Resistor [tolerance=±5% resistance=20k package="2512 [SMD]"]
  R2 = Resistor [tolerance=±5% resistance=10k package="2512 [SMD]"]
  R3 = Resistor [tolerance=±5% resistance=10k package="2512 [SMD]"]
  R5 = Resistor [tolerance=±5% resistance=100 package="2512 [SMD]"]
  R6 = Resistor [tolerance=±5% resistance=10k package="2512 [SMD]"]
  Q3 = Basic FET P-Channel [package="DPak [SMD]"]
  Q4 = Basic FET N-Channel [package="DPak [SMD]"]

nets:
  N1: -_+.pin1, R6.Pin_1, Q3.source
  GND: -_+.pin2, J1.pin3, R2.Pin_1, R3.Pin_1, Q4.source
  ADC: J1.pin1, R1.Pin_1, R2.Pin_0
  EN: J1.pin2, R5.Pin_1
  N2: R4.Pin_0, R6.Pin_0, Q3.Gate
  N3: R4.Pin_1, Q4.drain
  N4: R1.Pin_0, Q3.drain
  N5: R3.Pin_0, R5.Pin_0, Q4.Gate
