# Fritzing sketch circuit (saved by Fritzing 0.9.2b)
circuit board: 8.46667cm x 5.64444cm
breadboards: 1

parts:
  R1 = Resistor [tolerance=±5% resistance=10k package=THT]
  LED1 = LED - 5mm [color="Red (633nm)" package="5 mm [THT]"]
  Q1 = NPN-Transistor [package="TO92 [THT]"]
  R2 = Resistor [tolerance=±5% resistance=1k package=THT]

nets:
  EN: R1.Pin_0
  N1: R1.Pin_1, Q1.B, R2.Pin_0
  N2: LED1.cathode, Q1.C
  3.3V: LED1.anode
  GND: Q1.E, R2.Pin_1
