# Fritzing sketch rpi_transistor_test (saved by Fritzing 0.9.2b)
breadboards: 1

parts:
  Raspberry_Pi1 = Raspberry Pi 2
  Q1 = Basic FET N-Channel [part_number=ZVN3306 package="D2Pak [SMD]"]
  R1 = Resistor [tolerance=±5% resistance=330 package=THT]
  R2 = Resistor [tolerance=±5% resistance=10k package=THT]
  LED1 = LED - 3mm [color="Red (633nm)" package="3 mm [THT]"]
  R3 = Resistor [tolerance=±5% resistance=150 package=THT]

nets:
  GND: Raspberry_Pi1.GND, Q1.source, R2.Pin_1
  N1: Raspberry_Pi1.GPIO20, R1.Pin_0
  5V: Raspberry_Pi1.5V
  N2: Q1.Gate, R1.Pin_1, R2.Pin_0
  N3: Q1.drain, LED1.cathode
  N4: LED1.anode, R3.Pin_1
  3.3V: R3.Pin_0
